# Fritzing sketch fritzingSchemaWeerstation (saved by Fritzing 0.9.3b)
breadboards: 1

parts:
  R2 = Photocell (LDR) [package=THT]
  470-Ohm_NTC = Temperature Sensor (Thermistor) [thermistor_type=NTC package=THT]
  R3 = Resistor [tolerance=±5% resistance=10k package=THT]
  R4 = Resistor [tolerance=±5% resistance=470 package=THT]
  Part1 = Arduino Uno (Rev3)  # not connected
  Part2 = Arduino Board Ethernet

nets:
  N1: R2.pin_0, Part2.5V
  N2: R2.pin_1, R3.Pin_0, Part2.A1
  N3: 470-Ohm_NTC.pin_1, R4.Pin_0, Part2.A0
  N4: R3.Pin_1, R4.Pin_1, Part2.GND
